// Logisim project mem.circ as structural Verilog: 1 circuit, main circuit main
module main (
  input  [31:0] Data_Mem_Addr,
  input  [31:0] Data_Mem_In,
  input  ACCESS_BYTE,
  input  MEM_WRITE,
  input  CLOCK,
  output [31:0] Data_Mem_Out
);

  wire not_1_out;
  wire [1:0] byte_offset;
  wire [7:0] multiplexer_1_out, ram_1_data, ram_1_data_2, ram_1_data_3, ram_1_data_4;
  wire [31:0] bit_extender_1_out;
  wire [31:2] subtractor_1_out;

  Subtractor #(.width(32)) subtractor_1 (
    .a(Data_Mem_Addr), .b(32'h10010000), .out({subtractor_1_out, byte_offset}));  // open: bin, bout
  not not_1 (not_1_out, MEM_WRITE);
  RAM #(.addrWidth(24), .dataWidth(32), .bus("separate")) ram_1 (
    .addr(subtractor_1_out[25:2]), .din(Data_Mem_In),
    .data({ram_1_data_4, ram_1_data_3, ram_1_data_2, ram_1_data}), .str(MEM_WRITE), .clk(CLOCK),
    .ld(not_1_out));  // open: sel, clr
  Multiplexer #(.select(2), .width(8), .enable("false")) multiplexer_1 (
    .in0(ram_1_data_4), .in1(ram_1_data_3), .in2(ram_1_data_2), .in3(ram_1_data), .out(multiplexer_1_out),
    .sel(byte_offset));
  assign bit_extender_1_out = {{24{1'b0}}, multiplexer_1_out};  // Bit_Extender bit_extender_1
  Multiplexer #(.width(32), .enable("false")) multiplexer_2 (
    .in0({ram_1_data_4, ram_1_data_3, ram_1_data_2, ram_1_data}), .in1(bit_extender_1_out),
    .out(Data_Mem_Out), .sel(ACCESS_BYTE));

  // Notes on the sheet:
  //   These are INPUTS to the circuit
  //   #only load
  //   These are INPUTS to the circuit
  //   DO NOT CHANGE THE LOCATIONS OF THE INPUTS/OUTPUTS! IF YOU DO SO, YOU NEED TO MAKE SURE THE PINS ARE AT THE RIGHT PLACE!
  //   Yet again, the clock is not an actual clock, but an input, one that will be driven from a higher circuit
  //   Memory
  //   This is an OUTPUT to the circuit
endmodule
