// Logisim project alu.circ as structural Verilog: 1 circuit, main circuit main
module main (
  input  [31:0] X,
  input  [31:0] Y,
  input  [5:0] Switch__S,
  output Signed_Overflow,
  output [31:0] RESULT,
  output Equal
);

  wire add_overflow, and_3_out, and_4_out, comparator_3_eq, comparator_6_eq, comparator_7_eq,
       comparator_8_lt, comparator_9_lt, if_add_funct, if_sub_funct, not_1_out, not_2_out,
       same_input_top_bit, sub_overflow, xor_1_out, xor_2_out, xor_3_out;
  wire [4:0] bit_extender_1_out, bit_extender_3_out, bit_extender_6_out;
  wire [15:0] bit_extender_2_out, bit_extender_4_out, or_2_out, shifter_2_out, shifter_4_out;
  wire [31:0] add, addu, \and , bitpal, lfsr, \or , sll, slt, sltu, sra, srl, sub, subu;

  Comparator #(.width(5)) comparator_1 (
    .a({Switch__S[5], Switch__S[3:0]}), .b(5'b10000), .eq(if_add_funct));  // open: gt, lt
  Comparator #(.width(5)) comparator_2 (
    .a({Switch__S[5], Switch__S[3:0]}), .b(5'b10010), .eq(if_sub_funct));  // open: gt, lt
  Adder #(.width(32)) adder_1 (.a(X), .b(Y), .out(addu));  // open: cin, cout
  assign \and  = X & Y;  // AND_Gate and_1, 32 bits wide
  Bit_Extender #(.in_width(32), .out_width(5)) bit_extender_1 (.in(Y), .out(bit_extender_1_out));
  Adder #(.width(32)) adder_2 (.a(X), .b(Y), .out(add));  // open: cin, cout
  Bit_Extender #(.in_width(32)) bit_extender_2 (.in(X), .out(bit_extender_2_out));
  Shifter #(.width(32)) shifter_1 (.in(X), .\dist (bit_extender_1_out), .out(sll));
  Comparator #(.width(1)) comparator_3 (.a(add[31]), .b(X[31]), .eq(comparator_3_eq));  // open: gt, lt
  not not_1 (not_1_out, comparator_3_eq);
  and and_2 (add_overflow, not_1_out, same_input_top_bit);
  Shifter #(.width(16), .shift("lr")) shifter_2 (.in(bit_extender_2_out), .\dist (4'b0001), .out(shifter_2_out));
  xor xor_1 (xor_1_out, bit_extender_2_out[0], bit_extender_2_out[2]);
  Subtractor #(.width(32)) subtractor_1 (.a(X), .b(Y), .out(subu));  // open: bin, bout
  assign \or  = X | Y;  // OR_Gate or_1, 32 bits wide
  Shifter #(.width(32), .shift("lr")) shifter_3 (.in(X), .\dist (bit_extender_3_out), .out(srl));
  Bit_Extender #(.in_width(32), .out_width(5)) bit_extender_3 (.in(Y), .out(bit_extender_3_out));
  Comparator #(.width(1)) comparator_4 (.a(Y[31]), .b(X[31]), .eq(same_input_top_bit));  // open: gt, lt
  Comparator #(.width(32)) comparator_5 (.a(X), .b(Y), .eq(Equal));  // open: gt, lt
  xor xor_2 (xor_2_out, xor_1_out, bit_extender_2_out[3]);
  xor xor_3 (xor_3_out, xor_2_out, bit_extender_2_out[5]);
  assign bit_extender_4_out = {{15{1'b0}}, xor_3_out};  // Bit_Extender bit_extender_4
  and and_3 (and_3_out, if_add_funct, add_overflow);
  and and_4 (and_4_out, if_sub_funct, sub_overflow);
  Comparator #(.width(16)) comparator_6 (
    .a({X[0], X[1], X[2], X[3], X[4], X[5], X[6], X[7], X[8], X[9], X[10], X[11], X[12], X[13], X[14], X[15]}),
    .b(X[31:16]), .eq(comparator_6_eq));  // open: gt, lt
  assign bitpal = {{31{1'b0}}, comparator_6_eq};  // Bit_Extender bit_extender_5
  Multiplexer #(.select(5), .width(32)) multiplexer_1 (
    .in0(sll), .in2(srl), .in3(sra), .in16(add), .in17(addu), .in18(sub), .in19(subu), .in20(\and ),
    .in21(\or ), .in26(slt), .in27(sltu), .in30(bitpal), .in31(lfsr), .out(RESULT),
    .sel({Switch__S[5], Switch__S[3:0]}));  // open: in1, in4, in5, in6, in7, in8, in9, in10, in11, in12, in13, in14, in15, in22, in23, in24, in25, in28, in29, en
  Bit_Extender #(.in_width(32), .out_width(5)) bit_extender_6 (.in(Y), .out(bit_extender_6_out));
  Subtractor #(.width(32)) subtractor_2 (.a(X), .b(Y), .out(sub));  // open: bin, bout
  Comparator #(.width(1)) comparator_7 (.a(sub[31]), .b(Y[31]), .eq(comparator_7_eq));  // open: gt, lt
  not not_2 (not_2_out, same_input_top_bit);
  Shifter #(.width(16)) shifter_4 (.in(bit_extender_4_out), .\dist (4'b1111), .out(shifter_4_out));
  assign or_2_out = shifter_4_out | shifter_2_out;  // OR_Gate or_2, 16 bits wide
  or or_3 (Signed_Overflow, and_3_out, and_4_out);
  Comparator #(.width(32), .mode("unsigned")) comparator_8 (.a(X), .b(Y), .lt(comparator_8_lt));  // open: gt, eq
  Comparator #(.width(32)) comparator_9 (.a(X), .b(Y), .lt(comparator_9_lt));  // open: gt, eq
  and and_5 (sub_overflow, comparator_7_eq, not_2_out);
  assign lfsr = {{16{1'b0}}, or_2_out};  // Bit_Extender bit_extender_7
  assign sltu = {{31{1'b0}}, comparator_8_lt};  // Bit_Extender bit_extender_8
  assign slt = {{31{1'b0}}, comparator_9_lt};  // Bit_Extender bit_extender_9
  Shifter #(.width(32), .shift("ar")) shifter_5 (.in(X), .\dist (bit_extender_6_out), .out(sra));

  // Other names for the same wires on the sheet: x_input[31:0] = X; add_top_bit = add[31]; sub_top_bit = sub[31];
  //   switch[4:0] = {Switch__S[5], Switch__S[3:0]}; y_input[31:0] = Y

  // Notes on the sheet:
  //   INPUTS to your circuit
  //   INPUT to your circuit
  //   # bitpal
  //   # x[31:16] = x[0:15] ?
  //   # lfsr
  //    ALU Functions for Mux without Overflow
  //    ALU Functions for Mux with Overflow
  //    ALU Functions for Output Equal
  //   New ALU Functions
  //   DON'T CHANGE THE INPUTS AND OUTPUTS! IF YOU DO SO, YOU NEED TO MAKE SURE THE PINS ARE IN THE RIGHT PLACES!
  //   OUTPUTS of your circuit
endmodule
