// Logisim project cpu.circ as structural Verilog: 1 circuit, main circuit main
module main (
  input  [31:0] RS_READ_VALUE,
  input  [31:0] RT_READ_VALUE,
  input  [31:0] INSTRUCTION,
  input  CLOCK,
  input  RESET,
  output [31:0] t0,
  output [31:0] t1,
  output [31:0] t2,
  output [31:0] t3,
  output [4:0] RS,
  output [4:0] RT,
  output [4:0] Write_Register,
  output [31:0] RD_WRITE_VALUE,
  output RD_WRITE_ENABLE,
  output [23:0] FETCH_ADDRESS
);

  wire alu_if_equal, alu_if_overflow, alu_src, and_1_out, and_2_out, and_3_out, and_4_out, and_5_out, branch,
       branch_taken, byte_access, call_addu_in_alu, comparator_14_gt, comparator_15_lt, comparator_16_gt,
       comparator_17_lt, comparator_18_eq, comparator_19_eq, comparator_20_eq, comparator_21_eq,
       comparator_22_gt, comparator_23_lt, if_addiu, if_andi, if_beq, if_bne, if_jal, if_jr, if_jump, if_lb,
       if_lbu, if_lui, if_lw, if_ori, if_sll, if_sra, if_srl, if_sw, jump, mem_to_reg, nop, not_1_out,
       or_5_out, or_6_out, or_7_out, or_8_out, or_10_out, r_type, reg_in_cpu_write, reg_write, shift_type;
  wire [4:0] reg_written_to;
  wire [5:0] alu_control, alu_op, funct, multiplexer_13_out, multiplexer_14_out, multiplexer_19_out;
  wire [7:0] bit_extender_5_out;
  wire [15:6] immediate;
  wire [23:0] adder_1_out, adder_2_out, bit_extender_3_out, multiplexer_7_out, multiplexer_12_out, next_pc,
       subtractor_1_out, subtractor_2_out, subtractor_3_out;
  wire [31:0] alu_result, bit_extender_4_out, bit_extender_6_out, bit_extender_7_out, main_2_data_mem_out,
       mem_result, multiplexer_1_out, multiplexer_4_out, multiplexer_8_out, multiplexer_9_out,
       multiplexer_10_out, multiplexer_15_out, multiplexer_16_out, multiplexer_20_out, read_data_1,
       read_data_2, rs_value_selected, rt_value_selected, signed_extd_imm, zero_extd_imm;
  wire [31:26] instruction_t;

  Comparator #(.width(6), .mode("unsigned")) comparator_1 (
    .a(instruction_t), .b({6{1'b0}}), .eq(r_type));  // open: gt, lt
  Comparator #(.width(6), .mode("unsigned")) comparator_2 (
    .a(instruction_t), .b(6'b001001), .eq(if_addiu));  // open: gt, lt
  Comparator #(.width(6), .mode("unsigned")) comparator_3 (
    .a(instruction_t), .b(6'b001100), .eq(if_andi));  // open: gt, lt
  Comparator #(.width(6), .mode("unsigned")) comparator_4 (
    .a(instruction_t), .b(6'b001101), .eq(if_ori));  // open: gt, lt
  Comparator #(.width(6), .mode("unsigned")) comparator_5 (
    .a(instruction_t), .b(6'b001111), .eq(if_lui));  // open: gt, lt
  Comparator #(.width(6), .mode("unsigned")) comparator_6 (
    .a(instruction_t), .b(6'b100000), .eq(if_lb));  // open: gt, lt
  Comparator #(.width(6), .mode("unsigned")) comparator_7 (
    .a(instruction_t), .b(6'b100100), .eq(if_lbu));  // open: gt, lt
  Comparator #(.width(6), .mode("unsigned")) comparator_8 (
    .a(instruction_t), .b(6'b100011), .eq(if_lw));  // open: gt, lt
  Comparator #(.width(6), .mode("unsigned")) comparator_9 (
    .a(instruction_t), .b(6'b101011), .eq(if_sw));  // open: gt, lt
  Comparator #(.width(6), .mode("unsigned")) comparator_10 (
    .a(instruction_t), .b(6'b000100), .eq(if_beq));  // open: gt, lt
  Comparator #(.width(6), .mode("unsigned")) comparator_11 (
    .a(instruction_t), .b(6'b000101), .eq(if_bne));  // open: gt, lt
  Comparator #(.width(6), .mode("unsigned")) comparator_12 (
    .a(instruction_t), .b(6'b000010), .eq(if_jump));  // open: gt, lt
  Comparator #(.width(6), .mode("unsigned")) comparator_13 (
    .a(instruction_t), .b(6'b000011), .eq(if_jal));  // open: gt, lt
  Register #(.width(24)) register_1 (.D(next_pc), .Q(FETCH_ADDRESS), .clk(CLOCK));  // open: en, clr
  not not_1 (not_1_out, alu_if_equal);
  Multiplexer #(.width(32), .enable("false")) multiplexer_1 (
    .in0(alu_result), .in1(mem_result), .out(multiplexer_1_out), .sel(mem_to_reg));
  Comparator #(.width(5), .mode("unsigned")) comparator_14 (
    .a(RS), .b(5'b00111), .gt(comparator_14_gt));  // open: eq, lt
  Comparator #(.width(5), .mode("unsigned")) comparator_15 (
    .a(RS), .b(5'b01100), .lt(comparator_15_lt));  // open: gt, eq
  Comparator #(.width(5), .mode("unsigned")) comparator_16 (
    .a(RT), .b(5'b00111), .gt(comparator_16_gt));  // open: eq, lt
  Comparator #(.width(5), .mode("unsigned")) comparator_17 (
    .a(RT), .b(5'b01100), .lt(comparator_17_lt));  // open: gt, eq
  and and_1 (and_1_out, if_beq, alu_if_equal);
  and and_2 (and_2_out, not_1_out, if_bne);
  Multiplexer #(.width(5), .enable("false")) multiplexer_2 (
    .in0(reg_written_to), .in1({5{1'b1}}), .out(Write_Register), .sel(if_jal));
  or or_1 (jump, if_jal, if_jr, if_jump);
  regfile_main main_1 (
    .Read_register_1(RS[1:0]), .Read_register_2(RT[1:0]), .write_register(reg_written_to[1:0]),
    .write_data(multiplexer_1_out), .t0_Value(t0), .t1_Value(t1), .t2_Value(t2), .t3_Value(t3),
    .RegWrite(and_3_out), .clock(CLOCK), .Read_Data_1(read_data_1), .Read_Data_2(read_data_2));
  and and_3 (and_3_out, reg_in_cpu_write, reg_write);
  and and_4 (and_4_out, comparator_14_gt, comparator_15_lt);
  and and_5 (and_5_out, comparator_16_gt, comparator_17_lt);
  Multiplexer #(.width(6), .enable("false")) multiplexer_3 (.in0(alu_op), .in1(funct), .out(alu_control), .sel(r_type));
  assign signed_extd_imm = {{16{immediate[15]}}, {immediate, funct}};  // Bit_Extender bit_extender_1
  assign zero_extd_imm = {{16{1'b0}}, {immediate, funct}};  // Bit_Extender bit_extender_2
  Adder #(.width(24)) adder_1 (.a(FETCH_ADDRESS), .b(24'h1), .out(adder_1_out));  // open: cin, cout
  assign bit_extender_3_out = {{8{immediate[15]}}, {immediate, funct}};  // Bit_Extender bit_extender_3
  or or_2 (branch_taken, and_1_out, and_2_out);
  or or_3 (call_addu_in_alu, if_addiu, if_lb, if_lbu, if_lw, if_sw);
  or or_4 (branch, if_beq, if_bne);
  or or_5 (or_5_out, if_lbu, if_lb);
  Adder #(.width(24)) adder_2 (.a(FETCH_ADDRESS), .b(bit_extender_3_out), .out(adder_2_out));  // open: cin, cout
  Multiplexer #(.width(32), .enable("false")) multiplexer_4 (
    .in0(INSTRUCTION), .in1({32{1'b0}}), .out(multiplexer_4_out), .sel(nop));
  Comparator #(.width(6), .mode("unsigned")) comparator_18 (
    .a(funct), .b(6'b001000), .eq(comparator_18_eq));  // open: gt, lt
  Multiplexer #(.width(32), .enable("false")) multiplexer_5 (
    .in0(RS_READ_VALUE), .in1(read_data_1), .out(rs_value_selected), .sel(and_4_out));
  Multiplexer #(.width(32), .enable("false")) multiplexer_6 (
    .in0(RT_READ_VALUE), .in1(read_data_2), .out(rt_value_selected), .sel(and_5_out));
  Multiplexer #(.width(24), .enable("false")) multiplexer_7 (
    .in0(adder_1_out), .in1(adder_2_out), .out(multiplexer_7_out), .sel(branch_taken));
  Register #(.width(32)) pipeline_reg (
    .D(multiplexer_4_out), .Q({instruction_t, RS, RT, immediate, funct}), .clk(CLOCK));  // open: en, clr
  and and_6 (if_jr, r_type, comparator_18_eq);
  Multiplexer #(.width(32), .enable("false")) multiplexer_8 (
    .in0(rt_value_selected), .in1(signed_extd_imm), .out(multiplexer_8_out), .sel(alu_src));
  mem_main main_2 (
    .Data_Mem_Addr(alu_result), .Data_Mem_In(rt_value_selected), .ACCESS_BYTE(or_5_out), .MEM_WRITE(if_sw),
    .CLOCK(CLOCK), .Data_Mem_Out(main_2_data_mem_out));
  Multiplexer #(.width(32), .enable("false")) multiplexer_9 (
    .in0(rs_value_selected), .in1(rt_value_selected), .out(multiplexer_9_out), .sel(shift_type));
  Multiplexer #(.width(32), .enable("false")) multiplexer_10 (
    .in0(multiplexer_8_out), .in1(bit_extender_4_out), .out(multiplexer_10_out), .sel(shift_type));
  or or_6 (or_6_out, if_jump, if_jal);
  Subtractor #(.width(24)) subtractor_1 (
    .a({RS[2:0], RT, immediate, funct}), .b(24'h100000), .out(subtractor_1_out));  // open: bin, bout
  Multiplexer #(.width(5), .enable("false")) multiplexer_11 (
    .in0(RT), .in1(immediate[15:11]), .out(reg_written_to), .sel(r_type));
  assign bit_extender_4_out = {{27{1'b0}}, immediate[10:6]};  // Bit_Extender bit_extender_4
  Bit_Extender #(.in_width(32), .out_width(8)) bit_extender_5 (.in(main_2_data_mem_out), .out(bit_extender_5_out));
  Multiplexer #(.width(24), .enable("false")) multiplexer_12 (
    .in0(multiplexer_7_out), .in1(subtractor_1_out), .out(multiplexer_12_out), .sel(or_6_out));
  Subtractor #(.width(24)) subtractor_2 (.a(FETCH_ADDRESS), .b(24'h100000), .out(subtractor_2_out));  // open: bin, bout
  assign bit_extender_6_out = {{8{1'b0}}, subtractor_2_out};  // Bit_Extender bit_extender_6
  Multiplexer #(.width(6), .enable("false")) multiplexer_13 (
    .in0({6{1'b0}}), .in1(6'b100101), .out(multiplexer_13_out), .sel(if_ori));
  Comparator #(.width(6), .mode("unsigned")) comparator_19 (
    .a(funct), .b({6{1'b0}}), .eq(comparator_19_eq));  // open: gt, lt
  Comparator #(.width(6), .mode("unsigned")) comparator_20 (
    .a(funct), .b(6'b000010), .eq(comparator_20_eq));  // open: gt, lt
  Comparator #(.width(6), .mode("unsigned")) comparator_21 (
    .a(funct), .b(6'b000011), .eq(comparator_21_eq));  // open: gt, lt
  assign bit_extender_7_out = {{24{bit_extender_5_out[7]}}, bit_extender_5_out};  // Bit_Extender bit_extender_7
  or or_7 (or_7_out, if_beq, if_bne, if_jump, if_jr);
  or or_8 (or_8_out, r_type, jump, branch);
  Multiplexer #(.width(6), .enable("false")) multiplexer_14 (
    .in0(multiplexer_13_out), .in1(6'b100100), .out(multiplexer_14_out), .sel(if_andi));
  or or_9 (byte_access, if_lb, if_lbu);
  Multiplexer #(.width(32), .enable("false")) multiplexer_15 (
    .in0(multiplexer_9_out), .in1(zero_extd_imm), .out(multiplexer_15_out), .sel(if_lui));
  Multiplexer #(.width(32), .enable("false")) multiplexer_16 (
    .in0(multiplexer_10_out), .in1(32'h10), .out(multiplexer_16_out), .sel(if_lui));
  or or_10 (or_10_out, if_andi, if_ori);
  and and_7 (if_sll, r_type, comparator_19_eq);
  and and_8 (if_srl, r_type, comparator_20_eq);
  and and_9 (if_sra, r_type, comparator_21_eq);
  Multiplexer #(.width(32), .enable("false")) multiplexer_17 (
    .in0(main_2_data_mem_out), .in1(bit_extender_7_out), .out(mem_result), .sel(if_lb));
  Subtractor #(.width(24)) subtractor_3 (
    .a(rs_value_selected[23:0]), .b(24'h100000), .out(subtractor_3_out));  // open: bin, bout
  Multiplexer #(.width(32), .enable("false")) multiplexer_18 (
    .in0(alu_result), .in1(bit_extender_6_out), .out(RD_WRITE_VALUE), .sel(if_jal));
  or or_11 (nop, jump, branch_taken);
  not not_2 (reg_write, or_7_out);
  or or_12 (mem_to_reg, if_lb, if_lbu, if_lw);
  not not_3 (alu_src, or_8_out);
  Multiplexer #(.width(6), .enable("false")) multiplexer_19 (
    .in0(multiplexer_14_out), .in1(6'b100001), .out(multiplexer_19_out), .sel(call_addu_in_alu));
  Comparator #(.width(5), .mode("unsigned")) comparator_22 (
    .a(reg_written_to), .b(5'b00111), .gt(comparator_22_gt));  // open: eq, lt
  Comparator #(.width(5), .mode("unsigned")) comparator_23 (
    .a(reg_written_to), .b(5'b01100), .lt(comparator_23_lt));  // open: gt, eq
  Multiplexer #(.width(32), .enable("false")) multiplexer_20 (
    .in0(multiplexer_16_out), .in1(zero_extd_imm), .out(multiplexer_20_out), .sel(or_10_out));
  Multiplexer #(.width(24), .enable("false")) multiplexer_21 (
    .in0(multiplexer_12_out), .in1(subtractor_3_out), .out(next_pc), .sel(if_jr));
  Multiplexer #(.width(6), .enable("false")) multiplexer_22 (
    .in0(multiplexer_19_out), .in1(instruction_t), .out(alu_op), .sel(r_type));
  and and_10 (reg_in_cpu_write, comparator_22_gt, comparator_23_lt);
  alu_main main_3 (
    .Switch__S(alu_control), .X(multiplexer_15_out), .Equal(alu_if_equal), .RESULT(alu_result),
    .Signed_Overflow(alu_if_overflow), .Y(multiplexer_20_out));
  or or_13 (shift_type, if_sll, if_srl, if_sra);
  LED led_1 (.in(alu_if_overflow));

  // Other names for the same wires on the sheet: immediate[5:0] = funct;
  //   instruction_t[25:0] = {RS, RT, immediate, funct}; jump_addr[25:0] = {RS, RT, immediate, funct};
  //   shamt[4:0] = immediate[10:6]; rd_reg[4:0] = immediate[15:11]; rt_reg[4:0] = RT; rs_reg[4:0] = RS;
  //   opcode[5:0] = instruction_t; mem_write = if_sw; out_write_reg[4:0] = Write_Register;
  //   out_write_value[31:0] = RD_WRITE_VALUE; rd_src = r_type; rs_value[31:0] = RS_READ_VALUE;
  //   rt_value[31:0] = RT_READ_VALUE; write_enable = RD_WRITE_ENABLE

  // Notes on the sheet:
  //   These are outputs/inputs from run.circ
  //   EX Stage
  //    generate control signals
  //    split the instruction into parts
  //    generate control signals
  //   read from and write to register file
  //   ALU
  //   Memory
  //   ajust PC value
  //   write to outside register file
  //   These are outputs to run.circ
  //   IF Stage
  //   00 for lui
  //    # jal needs to write register!
endmodule
